// Logisim project 1 Bit ALU v2.circ as structural Verilog: 2 circuits, main circuit main
module main (
  input  A,
  input  B,
  input  C,
  input  F2,
  input  F1,
  input  F0,
  output Y0,
  output Y1
);

  wire and_or_with_mux_1_b_2, and_or_with_mux_1_out_3, and_or_with_mux_1_out_5, and_or_with_mux_1_out_6,
       xor_1_out, xor_2_out;

  and_or_with_mux and_or_with_mux_1 (
    .A(A), .out_3(and_or_with_mux_1_out_3), .B_2(and_or_with_mux_1_b_2), .out_5(and_or_with_mux_1_out_5),
    .out_6(and_or_with_mux_1_out_6), .B(B));
  Multiplexer #(.select(3)) multiplexer_1 (
    .in0(and_or_with_mux_1_out_3), .in1(and_or_with_mux_1_out_3), .in2(and_or_with_mux_1_b_2),
    .in3(and_or_with_mux_1_b_2), .in4(and_or_with_mux_1_out_3), .in5(and_or_with_mux_1_out_5),
    .in6(and_or_with_mux_1_b_2), .in7(and_or_with_mux_1_out_6), .out(Y1), .sel({F1, F0, C}), .en(F2));
  xor xor_1 (xor_1_out, A, B);
  xor xor_2 (xor_2_out, xor_1_out, C);
  Multiplexer #(.select(3)) multiplexer_2 (
    .in0(1'b0), .in1(and_or_with_mux_1_out_5), .in2(and_or_with_mux_1_out_3), .in3(xor_1_out),
    .in4(xor_1_out), .in5(xor_1_out), .in6(xor_2_out), .in7(xor_2_out), .out(Y0), .sel({F2, F1, F0}),
    .en(1'b1));

  // Notes on the sheet:
  //   F2
  //   F1
  //   C
  //   F0
  //   F2
  //   F0
  //   F1
endmodule

module and_or_with_mux (
  input  A,
  input  B,
  output out_3,
  output B_2,
  output out_5,
  output out_6
);

  Multiplexer multiplexer_1 (.in0(1'b0), .in1(B), .out(out_3), .sel(A));  // open: en
  Multiplexer multiplexer_2 (.in0(B), .in1(1'b0), .out(B_2), .sel(A));  // open: en
  Multiplexer multiplexer_3 (.in0(B), .in1(1'b1), .out(out_5), .sel(A));  // open: en
  Multiplexer multiplexer_4 (.in0(1'b1), .in1(B), .out(out_6), .sel(A));  // open: en

  // Notes on the sheet:
  //   B
  //   A.B
  //   B
  //   A'.B
  //   A+B
  //   B
  //   A'+B
endmodule
