// Logisim project BUS ALU v2.circ as structural Verilog
module main (
  input  CI_prime,
  input  in_2,
  input  [3:0] in_3,
  input  in_4,
  input  _1___Reset,
  input  in_6,
  input  in_7,
  input  in_8,
  input  in_9,
  output [3:0] out_10
);

  wire _2_0_out, clock_1_out;
  wire [3:0] n4_bit_alu_1_out_6, register_4035_1_out_9, register_4076_1_out_10, tri_state_buffer_1_out_12;

  Tri_State_Buffer tri_state_buffer_1 (
    .in_1(in_4), .in_2(in_6), .out_9(tri_state_buffer_1_out_12[3]), .in_3(in_4), .in_4(in_7),
    .out_10(tri_state_buffer_1_out_12[2]), .in_5(in_4), .in_6(in_8), .out_11(tri_state_buffer_1_out_12[1]),
    .in_7(in_4), .in_8(in_9), .out_12(tri_state_buffer_1_out_12[0]));
  Multiplexer #(.width(4)) multiplexer_1 (
    .in0(tri_state_buffer_1_out_12), .in1(register_4076_1_out_10), .out(out_10), .sel(in_4), .en(1'b1));
  _4_bit_ALU u_4_bit_alu_1 (
    .in_1(out_10), .in_2(register_4035_1_out_9), .in_5(in_3), .out_6(n4_bit_alu_1_out_6), .in_4(in_2),
    .in_3(CI_prime));
  Register_4076 register_4076_1 (
    .in_6(_1___Reset), .in_2(n4_bit_alu_1_out_6[3]), .in_3(n4_bit_alu_1_out_6[2]),
    .in_4(n4_bit_alu_1_out_6[1]), .in_5(n4_bit_alu_1_out_6[0]), .out_7(register_4076_1_out_10[3]),
    .out_8(register_4076_1_out_10[2]), .out_9(register_4076_1_out_10[1]), .out_10(register_4076_1_out_10[0]),
    .in_1(_2_0_out));
  Clock clock_1 (.out(clock_1_out));
  Register_4035 register_4035_1 (
    .in_1(clock_1_out), .in_2(out_10[3]), .in_3(out_10[2]), .in_4(out_10[1]), .in_5(out_10[0]),
    .out_6(register_4035_1_out_9[3]), .out_7(register_4035_1_out_9[2]), .out_8(register_4035_1_out_9[1]),
    .out_9(register_4035_1_out_9[0]));
  Clock _2_0 (.out(_2_0_out));

  // Notes on the sheet:
  //   Clock
  //   Clock
endmodule

module Tri_State_Buffer (
  input  in_1,
  input  in_2,
  input  in_3,
  input  in_4,
  input  in_5,
  input  in_6,
  input  in_7,
  input  in_8,
  output out_9,
  output out_10,
  output out_11,
  output out_12
);

  Transistor transistor_1 (.in(in_2), .out(out_9), .gate(in_1));
  Transistor transistor_2 (.in(in_4), .out(out_10), .gate(in_3));
  Transistor transistor_3 (.in(in_6), .out(out_11), .gate(in_5));
  Transistor transistor_4 (.in(in_8), .out(out_12), .gate(in_7));
endmodule

module Register_4035 (
  input  in_1,
  input  in_2,
  input  in_3,
  input  in_4,
  input  in_5,
  output out_6,
  output out_7,
  output out_8,
  output out_9
);

  D_Flip_Flop #(.trigger("falling")) d_ff_1 (.clk(in_1), .D(in_2), .Q(out_6));  // open: Qn, preset, en, reset
  D_Flip_Flop #(.trigger("falling")) d_ff_2 (.clk(in_1), .D(in_3), .Q(out_7));  // open: Qn, preset, en, reset
  D_Flip_Flop #(.trigger("falling")) d_ff_3 (.clk(in_1), .D(in_4), .Q(out_8));  // open: Qn, preset, en, reset
  D_Flip_Flop #(.trigger("falling")) d_ff_4 (.clk(in_1), .D(in_5), .Q(out_9));  // open: Qn, preset, en, reset
endmodule

module _4_bit_ALU (
  input  [3:0] in_1,
  input  [3:0] in_2,
  input  in_3,
  input  in_4,
  input  [3:0] in_5,
  output [3:0] out_6
);

  wire [3:0] high_1_out_3, high_1_out_4, high_1_out_5, high_1_out_6, high_1_out_7, high_1_out_8,
       high_1_out_9, high_1_out_10, high_1_out_11, high_1_out_12, high_1_out_13, high_1_out_14,
       high_1_out_15, high_1_out_16, high_1_out_17, high_1_out_18, low_1_out_4, low_1_out_5, low_1_out_6,
       low_1_out_7, low_1_out_8, low_1_out_9, low_1_out_10, low_1_out_11, low_1_out_12, low_1_out_13,
       low_1_out_14, low_1_out_15, low_1_out_16, low_1_out_17, low_1_out_18, low_1_out_19;

  LOW low_1 (
    .in_1(in_1), .in_2(in_2), .in_3(in_3), .out_4(low_1_out_4), .out_5(low_1_out_5), .out_6(low_1_out_6),
    .out_7(low_1_out_7), .out_8(low_1_out_8), .out_9(low_1_out_9), .out_10(low_1_out_10),
    .out_11(low_1_out_11), .out_12(low_1_out_12), .out_13(low_1_out_13), .out_14(low_1_out_14),
    .out_15(low_1_out_15), .out_16(low_1_out_16), .out_17(low_1_out_17), .out_18(low_1_out_18),
    .out_19(low_1_out_19));
  High high_1 (
    .in_1(in_1), .in_2(in_2), .out_3(high_1_out_3), .out_4(high_1_out_4), .out_5(high_1_out_5),
    .out_6(high_1_out_6), .out_7(high_1_out_7), .out_8(high_1_out_8), .out_9(high_1_out_9),
    .out_10(high_1_out_10), .out_11(high_1_out_11), .out_12(high_1_out_12), .out_13(high_1_out_13),
    .out_14(high_1_out_14), .out_15(high_1_out_15), .out_16(high_1_out_16), .out_17(high_1_out_17),
    .out_18(high_1_out_18));
  Multiplexer #(.select(5), .width(4)) multiplexer_1 (
    .in0(low_1_out_4), .in1(low_1_out_5), .in2(low_1_out_6), .in3(low_1_out_7), .in4(low_1_out_8),
    .in5(low_1_out_9), .in6(low_1_out_10), .in7(low_1_out_11), .in8(low_1_out_12), .in9(low_1_out_13),
    .in10(low_1_out_14), .in11(low_1_out_15), .in12(low_1_out_16), .in13(low_1_out_17), .in14(low_1_out_18),
    .in15(low_1_out_19), .in16(high_1_out_3), .in17(high_1_out_4), .in18(high_1_out_5), .in19(high_1_out_6),
    .in20(high_1_out_7), .in21(high_1_out_8), .in22(high_1_out_9), .in23(high_1_out_10),
    .in24(high_1_out_11), .in25(high_1_out_12), .in26(high_1_out_13), .in27(high_1_out_14),
    .in28(high_1_out_15), .in29(high_1_out_16), .in30(high_1_out_17), .in31(high_1_out_18), .out(out_6),
    .sel({in_4, in_5}), .en(1'b1));
endmodule

module Register_4076 (
  input  in_1,
  input  in_2,
  input  in_3,
  input  in_4,
  input  in_5,
  input  in_6,
  output out_7,
  output out_8,
  output out_9,
  output out_10
);

  D_Flip_Flop #(.trigger("falling")) d_ff_1 (.clk(in_1), .D(in_2), .Q(out_7), .reset(in_6));  // open: Qn, preset, en
  D_Flip_Flop #(.trigger("falling")) d_ff_2 (.clk(in_1), .D(in_3), .Q(out_8), .reset(in_6));  // open: Qn, preset, en
  D_Flip_Flop #(.trigger("falling")) d_ff_3 (.clk(in_1), .D(in_4), .Q(out_9), .reset(in_6));  // open: Qn, preset, en
  D_Flip_Flop #(.trigger("falling")) d_ff_4 (.clk(in_1), .D(in_5), .Q(out_10), .reset(in_6));  // open: Qn, preset, en
endmodule

module Not (
  input  in_1,
  input  in_2,
  input  in_3,
  input  in_4,
  output out_5,
  output out_6,
  output out_7,
  output out_8
);

  Multiplexer multiplexer_1 (.in0(1'b1), .in1(1'b0), .out(out_5), .sel(in_1));  // open: en
  Multiplexer multiplexer_2 (.in0(1'b1), .in1(1'b0), .out(out_6), .sel(in_2));  // open: en
  Multiplexer multiplexer_3 (.in0(1'b1), .in1(1'b0), .out(out_7), .sel(in_3));  // open: en
  Multiplexer multiplexer_4 (.in0(1'b1), .in1(1'b0), .out(out_8), .sel(in_4));  // open: en
endmodule

module Or (
  input  in_1,
  input  in_2,
  input  in_3,
  input  in_4,
  input  in_5,
  input  in_6,
  input  in_7,
  input  in_8,
  output out_9,
  output out_10,
  output out_11,
  output out_12
);

  Multiplexer multiplexer_1 (.in0(in_1), .in1(1'b1), .out(out_9), .sel(in_5));  // open: en
  Multiplexer multiplexer_2 (.in0(in_2), .in1(1'b1), .out(out_10), .sel(in_6));  // open: en
  Multiplexer multiplexer_3 (.in0(in_3), .in1(1'b1), .out(out_11), .sel(in_7));  // open: en
  Multiplexer multiplexer_4 (.in0(in_4), .in1(1'b1), .out(out_12), .sel(in_8));  // open: en
endmodule

module And (
  input  in_1,
  input  in_2,
  input  in_3,
  input  in_4,
  input  in_5,
  input  in_6,
  input  in_7,
  input  in_8,
  output out_9,
  output out_10,
  output out_11,
  output out_12
);

  Multiplexer multiplexer_1 (.in0(1'b0), .in1(in_1), .out(out_9), .sel(in_5));  // open: en
  Multiplexer multiplexer_2 (.in0(1'b0), .in1(in_2), .out(out_10), .sel(in_6));  // open: en
  Multiplexer multiplexer_3 (.in0(1'b0), .in1(in_3), .out(out_11), .sel(in_7));  // open: en
  Multiplexer multiplexer_4 (.in0(1'b0), .in1(in_4), .out(out_12), .sel(in_8));  // open: en
endmodule

module Xor (
  input  [3:0] in_1,
  input  [3:0] in_2,
  output [3:0] out_3
);

  wire not_1_out_5, not_1_out_6, not_1_out_7, not_1_out_8, not_2_out_5, not_2_out_6, not_2_out_7, not_2_out_8;
  wire [3:0] and_1_out_9, and_2_out_9;

  Not not_1 (
    .in_1(in_1[0]), .in_2(in_1[1]), .in_3(in_1[2]), .in_4(in_1[3]), .out_5(not_1_out_5), .out_6(not_1_out_6),
    .out_7(not_1_out_7), .out_8(not_1_out_8));
  Not not_2 (
    .in_1(in_2[0]), .in_2(in_2[1]), .in_3(in_2[2]), .in_4(in_2[3]), .out_5(not_2_out_5), .out_6(not_2_out_6),
    .out_7(not_2_out_7), .out_8(not_2_out_8));
  And and_1 (
    .in_1(in_2[0]), .in_2(in_2[1]), .in_3(in_2[2]), .in_4(in_2[3]), .in_5(not_1_out_5), .in_6(not_1_out_6),
    .in_7(not_1_out_7), .in_8(not_1_out_8), .out_9(and_1_out_9[0]), .out_10(and_1_out_9[1]),
    .out_11(and_1_out_9[2]), .out_12(and_1_out_9[3]));
  And and_2 (
    .in_1(in_1[0]), .in_2(in_1[1]), .in_3(in_1[2]), .in_4(in_1[3]), .in_5(not_2_out_5), .in_6(not_2_out_6),
    .in_7(not_2_out_7), .in_8(not_2_out_8), .out_9(and_2_out_9[0]), .out_10(and_2_out_9[1]),
    .out_11(and_2_out_9[2]), .out_12(and_2_out_9[3]));
  Or or_1 (
    .in_5(and_1_out_9[0]), .in_6(and_1_out_9[1]), .in_7(and_1_out_9[2]), .in_8(and_1_out_9[3]),
    .out_9(out_3[0]), .out_10(out_3[1]), .out_11(out_3[2]), .out_12(out_3[3]), .in_1(and_2_out_9[0]),
    .in_3(and_2_out_9[2]), .in_4(and_2_out_9[3]), .in_2(and_2_out_9[1]));
endmodule

module High (
  input  [3:0] in_1,
  input  [3:0] in_2,
  output [3:0] out_3,
  output [3:0] out_4,
  output [3:0] out_5,
  output [3:0] out_6,
  output [3:0] out_7,
  output [3:0] out_8,
  output [3:0] out_9,
  output [3:0] out_10,
  output [3:0] out_11,
  output [3:0] out_12,
  output [3:0] out_13,
  output [3:0] out_14,
  output [3:0] out_15,
  output [3:0] out_16,
  output [3:0] out_17,
  output [3:0] out_18
);

  wire [3:0] and_2_out_9, or_1_out_9;

  Not not_1 (
    .in_1(in_1[0]), .in_2(in_1[1]), .in_3(in_1[2]), .in_4(in_1[3]), .out_5(out_3[0]), .out_6(out_3[1]),
    .out_7(out_3[2]), .out_8(out_3[3]));
  Or or_1 (
    .in_5(in_1[0]), .in_6(in_1[1]), .in_7(in_1[2]), .in_8(in_1[3]), .out_9(or_1_out_9[0]),
    .out_10(or_1_out_9[1]), .out_11(or_1_out_9[2]), .out_12(or_1_out_9[3]), .in_1(in_2[0]), .in_3(in_2[2]),
    .in_4(in_2[3]), .in_2(in_2[1]));
  And and_1 (
    .in_1(in_2[0]), .in_2(in_2[1]), .in_3(in_2[2]), .in_4(in_2[3]), .in_5(out_3[0]), .in_6(out_3[1]),
    .in_7(out_3[2]), .in_8(out_3[3]), .out_9(out_5[0]), .out_10(out_5[1]), .out_11(out_5[2]),
    .out_12(out_5[3]));
  And and_2 (
    .in_1(in_2[0]), .in_2(in_2[1]), .in_3(in_2[2]), .in_4(in_2[3]), .in_5(in_1[0]), .in_6(in_1[1]),
    .in_7(in_1[2]), .in_8(in_1[3]), .out_9(and_2_out_9[0]), .out_10(and_2_out_9[1]), .out_11(and_2_out_9[2]),
    .out_12(and_2_out_9[3]));
  Not not_2 (
    .in_1(in_2[0]), .in_2(in_2[1]), .in_3(in_2[2]), .in_4(in_2[3]), .out_5(out_8[0]), .out_6(out_8[1]),
    .out_7(out_8[2]), .out_8(out_8[3]));
  Xor xor_1 (.in_1(in_1), .in_2(in_2), .out_3(out_9));
  And and_3 (
    .in_1(out_8[0]), .in_2(out_8[1]), .in_3(out_8[2]), .in_4(out_8[3]), .in_5(in_1[0]), .in_6(in_1[1]),
    .in_7(in_1[2]), .in_8(in_1[3]), .out_9(out_10[0]), .out_10(out_10[1]), .out_11(out_10[2]),
    .out_12(out_10[3]));
  Or or_2 (
    .in_5(out_3[0]), .in_6(out_3[1]), .in_7(out_3[2]), .in_8(out_3[3]), .out_9(out_11[0]),
    .out_10(out_11[1]), .out_11(out_11[2]), .out_12(out_11[3]), .in_1(in_1[0]), .in_3(in_1[2]),
    .in_4(in_1[3]), .in_2(in_1[1]));
  Not not_3 (
    .in_1(out_10[0]), .in_2(out_10[1]), .in_3(out_10[2]), .in_4(out_10[3]), .out_5(out_12[0]),
    .out_6(out_12[1]), .out_7(out_12[2]), .out_8(out_12[3]));
  And and_4 (
    .in_1(in_2[0]), .in_2(in_2[1]), .in_3(in_2[2]), .in_4(in_2[3]), .in_5(in_1[0]), .in_6(in_1[1]),
    .in_7(in_1[2]), .in_8(in_1[3]), .out_9(out_14[0]), .out_10(out_14[1]), .out_11(out_14[2]),
    .out_12(out_14[3]));
  Or or_3 (
    .in_5(in_1[0]), .in_6(in_1[1]), .in_7(in_1[2]), .in_8(in_1[3]), .out_9(out_16[0]), .out_10(out_16[1]),
    .out_11(out_16[2]), .out_12(out_16[3]), .in_1(out_8[0]), .in_3(out_8[2]), .in_4(out_8[3]), .in_2(out_8[1]));
  Or or_4 (
    .in_5(in_1[0]), .in_6(in_1[1]), .in_7(in_1[2]), .in_8(in_1[3]), .out_9(out_17[0]), .out_10(out_17[1]),
    .out_11(out_17[2]), .out_12(out_17[3]), .in_1(in_2[0]), .in_3(in_2[2]), .in_4(in_2[3]), .in_2(in_2[1]));
  Not not_4 (
    .in_1(or_1_out_9[0]), .in_2(or_1_out_9[1]), .in_3(or_1_out_9[2]), .in_4(or_1_out_9[3]), .out_5(out_4[0]),
    .out_6(out_4[1]), .out_7(out_4[2]), .out_8(out_4[3]));
  Not not_5 (
    .in_1(and_2_out_9[0]), .in_2(and_2_out_9[1]), .in_3(and_2_out_9[2]), .in_4(and_2_out_9[3]),
    .out_5(out_7[0]), .out_6(out_7[1]), .out_7(out_7[2]), .out_8(out_7[3]));
  _3_4_bit_Subtractor u_3_4_bit_subtractor_1 ();

  assign out_6 = 4'b0000;
  assign out_13 = in_2;
  assign out_15 = 4'b1111;
  assign out_18 = in_1;

  // Other names for the same wires on the sheet: A_____B[3:0] = out_10; A_prime[3:0] = out_3; B_prime[3:0] = out_8
endmodule

module _1_bit_Not (
  input  in_1,
  output out_2
);

  Multiplexer multiplexer_1 (.in0(1'b1), .in1(1'b0), .out(out_2), .sel(in_1));  // open: en
endmodule

module _1_bit_Or (
  input  in_1,
  input  in_2,
  output out_3
);

  Multiplexer multiplexer_1 (.in0(in_1), .in1(1'b1), .out(out_3), .sel(in_2));  // open: en
endmodule

module _1_bit_And (
  input  in_1,
  input  in_2,
  output out_3
);

  Multiplexer multiplexer_1 (.in0(1'b0), .in1(in_1), .out(out_3), .sel(in_2));  // open: en
endmodule

module _1_bit_XOR (
  input  in_1,
  input  in_2,
  output out_3
);

  wire n1_bit_and_1_out_3, n1_bit_and_2_out_3, n1_bit_not_1_out_2, n1_bit_not_2_out_2;

  _1_bit_Not u_1_bit_not_1 (.in_1(in_1), .out_2(n1_bit_not_1_out_2));
  _1_bit_Not u_1_bit_not_2 (.in_1(in_2), .out_2(n1_bit_not_2_out_2));
  _1_bit_And u_1_bit_and_1 (.in_1(n1_bit_not_1_out_2), .in_2(in_2), .out_3(n1_bit_and_1_out_3));
  _1_bit_And u_1_bit_and_2 (.in_1(in_1), .in_2(n1_bit_not_2_out_2), .out_3(n1_bit_and_2_out_3));
  _1_bit_Or u_1_bit_or_1 (.in_1(n1_bit_and_1_out_3), .in_2(n1_bit_and_2_out_3), .out_3(out_3));
endmodule

module Half_Adder (
  input  in_1,
  input  in_2,
  output out_3,
  output out_4
);

  _1_bit_XOR u_1_bit_xor_1 (.in_1(in_1), .in_2(in_2), .out_3(out_3));
  _1_bit_And u_1_bit_and_1 (.in_1(in_1), .in_2(in_2), .out_3(out_4));
endmodule

module Half_Subtractor (
  input  in_1,
  input  in_2,
  output out_3,
  output out_4
);

  wire n1_bit_not_1_out_2;

  _1_bit_Not u_1_bit_not_1 (.in_1(in_1), .out_2(n1_bit_not_1_out_2));
  _1_bit_XOR u_1_bit_xor_1 (.in_1(in_1), .in_2(in_2), .out_3(out_3));
  _1_bit_And u_1_bit_and_1 (.in_1(n1_bit_not_1_out_2), .in_2(in_2), .out_3(out_4));
endmodule

module Full_Adder (
  input  in_1,
  input  in_2,
  input  in_3,
  output out_4,
  output out_5
);

  wire n1_bit_and_1_out_3, n1_bit_and_2_out_3, n1_bit_xor_1_out_3;

  _1_bit_XOR u_1_bit_xor_1 (.in_1(in_1), .in_2(in_2), .out_3(n1_bit_xor_1_out_3));
  _1_bit_XOR u_1_bit_xor_2 (.in_1(n1_bit_xor_1_out_3), .in_2(in_3), .out_3(out_4));
  _1_bit_And u_1_bit_and_1 (.in_1(in_3), .in_2(n1_bit_xor_1_out_3), .out_3(n1_bit_and_1_out_3));
  _1_bit_And u_1_bit_and_2 (.in_1(in_2), .in_2(in_1), .out_3(n1_bit_and_2_out_3));
  _1_bit_Or u_1_bit_or_1 (.in_1(n1_bit_and_1_out_3), .in_2(n1_bit_and_2_out_3), .out_3(out_5));

  // Notes on the sheet:
  //   S
endmodule

module Full_Subtractor (
  input  in_1,
  input  in_2,
  input  in_3,
  output out_4,
  output out_5
);

  wire n1_bit_and_1_out_3, n1_bit_and_2_out_3, n1_bit_not_1_out_2, n1_bit_not_2_out_2, n1_bit_xor_1_out_3;

  _1_bit_XOR u_1_bit_xor_1 (.in_1(in_1), .in_2(in_2), .out_3(n1_bit_xor_1_out_3));
  _1_bit_Not u_1_bit_not_1 (.in_1(n1_bit_xor_1_out_3), .out_2(n1_bit_not_1_out_2));
  _1_bit_Not u_1_bit_not_2 (.in_1(in_1), .out_2(n1_bit_not_2_out_2));
  _1_bit_XOR u_1_bit_xor_2 (.in_1(n1_bit_xor_1_out_3), .in_2(in_3), .out_3(out_4));
  _1_bit_And u_1_bit_and_1 (.in_1(in_3), .in_2(n1_bit_not_1_out_2), .out_3(n1_bit_and_1_out_3));
  _1_bit_And u_1_bit_and_2 (.in_1(in_2), .in_2(n1_bit_not_2_out_2), .out_3(n1_bit_and_2_out_3));
  _1_bit_Or u_1_bit_or_1 (.in_1(n1_bit_and_1_out_3), .in_2(n1_bit_and_2_out_3), .out_3(out_5));

  // Notes on the sheet:
  //   S
endmodule

module _2_4_bit_Adder (
  input  [3:0] in_1,
  input  [3:0] in_2,
  output [3:0] out_3,
  output out_4
);

  wire full_adder_1_out_5, full_adder_2_out_5, half_adder_1_out_4;

  Half_Adder half_adder_1 (.out_3(out_3[0]), .in_1(in_1[0]), .in_2(in_2[0]), .out_4(half_adder_1_out_4));
  Full_Adder full_adder_1 (
    .in_1(half_adder_1_out_4), .in_2(in_1[1]), .in_3(in_2[1]), .out_4(out_3[1]), .out_5(full_adder_1_out_5));
  Full_Adder full_adder_2 (
    .in_1(full_adder_1_out_5), .in_2(in_1[2]), .in_3(in_2[2]), .out_4(out_3[2]), .out_5(full_adder_2_out_5));
  Full_Adder full_adder_3 (.in_1(full_adder_2_out_5), .in_2(in_1[3]), .in_3(in_2[3]), .out_4(out_3[3]), .out_5(out_4));
endmodule

module _3_4_bit_Adder (
  input  [3:0] in_1,
  input  [3:0] in_2,
  input  [3:0] in_3,
  output MSB,
  output out_5,
  output [3:0] out_6
);

  wire n2_4_bit_adder_1_out_4, n2_4_bit_adder_2_out_4;
  wire [3:0] n2_4_bit_adder_1_out_3;

  _2_4_bit_Adder u_2_4_bit_adder_1 (
    .in_1(in_1), .in_2(in_2), .out_3(n2_4_bit_adder_1_out_3), .out_4(n2_4_bit_adder_1_out_4));
  _2_4_bit_Adder u_2_4_bit_adder_2 (
    .in_1(n2_4_bit_adder_1_out_3), .in_2(in_3), .out_3(out_6), .out_4(n2_4_bit_adder_2_out_4));
  Half_Adder half_adder_1 (.out_3(out_5), .in_1(n2_4_bit_adder_1_out_4), .in_2(n2_4_bit_adder_2_out_4), .out_4(MSB));
endmodule

module Trash (
  input  [3:0] in_1,
  input  [3:0] in_2,
  input  [3:0] in_3,
  input  [3:0] in_4,
  input  in_5,
  input  in_6,
  output [3:0] out_7,
  output [3:0] out_8,
  output [3:0] out_9,
  output [3:0] out_10,
  output out_11,
  output out_12
);

  wire n1_bit_xor_1_out_3;

  Xor xor_1 (.in_1(in_1), .in_2(in_2), .out_3(out_7));
  And and_1 (
    .in_1(in_2[0]), .in_2(in_2[1]), .in_3(in_2[2]), .in_4(in_2[3]), .in_5(in_1[0]), .in_6(in_1[1]),
    .in_7(in_1[2]), .in_8(in_1[3]), .out_9(out_10[0]), .out_10(out_10[1]), .out_11(out_10[2]),
    .out_12(out_10[3]));
  Adder #(.width(4)) adder_1 (.a(in_1), .b(in_2), .out(out_8), .cout(out_9[0]));  // open: cin
  _1_bit_XOR u_1_bit_xor_1 (.in_1(in_3[0]), .in_2(in_4[0]), .out_3(n1_bit_xor_1_out_3));
  _1_bit_XOR u_1_bit_xor_2 (.in_1(in_5), .in_2(in_6), .out_3(out_11));
  _1_bit_And u_1_bit_and_1 (.in_1(in_5), .in_2(in_6), .out_3(out_12));
  // Pins of 1 and 4 bits meet at out_9
endmodule

module _2_4_bit_Subtractor (
  input  [3:0] in_1,
  input  [3:0] in_2,
  output [3:0] out_3,
  output out_4
);

  wire full_subtractor_1_out_5, full_subtractor_2_out_5, half_subtractor_1_out_4;

  Half_Subtractor half_subtractor_1 (.in_1(in_1[0]), .in_2(in_2[0]), .out_3(out_3[0]), .out_4(half_subtractor_1_out_4));
  Full_Subtractor full_subtractor_1 (
    .in_1(half_subtractor_1_out_4), .in_2(in_1[1]), .in_3(in_2[1]), .out_4(out_3[1]),
    .out_5(full_subtractor_1_out_5));
  Full_Subtractor full_subtractor_2 (
    .in_1(full_subtractor_1_out_5), .in_2(in_1[2]), .in_3(in_2[2]), .out_4(out_3[2]),
    .out_5(full_subtractor_2_out_5));
  Full_Subtractor full_subtractor_3 (
    .in_1(full_subtractor_2_out_5), .in_2(in_1[3]), .in_3(in_2[3]), .out_4(out_3[3]), .out_5(out_4));
endmodule

module LOW (
  input  [3:0] in_1,
  input  [3:0] in_2,
  input  in_3,
  output [3:0] out_4,
  output [3:0] out_5,
  output [3:0] out_6,
  output [3:0] out_7,
  output [3:0] out_8,
  output [3:0] out_9,
  output [3:0] out_10,
  output [3:0] out_11,
  output [3:0] out_12,
  output [3:0] out_13,
  output [3:0] out_14,
  output [3:0] out_15,
  output [3:0] out_16,
  output [3:0] out_17,
  output [3:0] out_18,
  output [3:0] out_19
);

  wire [0:0] n1_bit_not_1_out_2;
  wire [3:0] A_B, A_B_prime, A_B_prime_t, A_B_t, and_2_out_9, not_1_out_5, not_2_out_5, not_3_out_5,
       or_2_out_9, subtractor_2_out;

  _1_bit_Not u_1_bit_not_1 (.in_1(in_3), .out_2(n1_bit_not_1_out_2[0]));
  _2_4_bit_Adder u_2_4_bit_adder_1 (.in_1(in_1), .in_2({3'b000, n1_bit_not_1_out_2[0]}), .out_3(out_4));  // open: out_4
  Or or_1 (
    .in_5(in_1[0]), .in_6(in_1[1]), .in_7(in_1[2]), .in_8(in_1[3]), .out_9(A_B[0]), .out_10(A_B[1]),
    .out_11(A_B[2]), .out_12(A_B[3]), .in_1(in_2[0]), .in_3(in_2[2]), .in_4(in_2[3]), .in_2(in_2[1]));
  Not not_1 (
    .in_1(in_2[0]), .in_2(in_2[1]), .in_3(in_2[2]), .in_4(in_2[3]), .out_5(not_1_out_5[0]),
    .out_6(not_1_out_5[1]), .out_7(not_1_out_5[2]), .out_8(not_1_out_5[3]));
  Not not_2 (
    .in_1(in_2[0]), .in_2(in_2[1]), .in_3(in_2[2]), .in_4(in_2[3]), .out_5(not_2_out_5[0]),
    .out_6(not_2_out_5[1]), .out_7(not_2_out_5[2]), .out_8(not_2_out_5[3]));
  Or or_2 (
    .in_5(in_1[0]), .in_6(in_1[1]), .in_7(in_1[2]), .in_8(in_1[3]), .out_9(or_2_out_9[0]),
    .out_10(or_2_out_9[1]), .out_11(or_2_out_9[2]), .out_12(or_2_out_9[3]), .in_1(in_2[0]), .in_3(in_2[2]),
    .in_4(in_2[3]), .in_2(in_2[1]));
  Not not_3 (
    .in_1(in_2[0]), .in_2(in_2[1]), .in_3(in_2[2]), .in_4(in_2[3]), .out_5(not_3_out_5[0]),
    .out_6(not_3_out_5[1]), .out_7(not_3_out_5[2]), .out_8(not_3_out_5[3]));
  And and_1 (
    .in_1(in_2[0]), .in_2(in_2[1]), .in_3(in_2[2]), .in_4(in_2[3]), .in_5(in_1[0]), .in_6(in_1[1]),
    .in_7(in_1[2]), .in_8(in_1[3]), .out_9(A_B_t[0]), .out_10(A_B_t[1]), .out_11(A_B_t[2]), .out_12(A_B_t[3]));
  _3_4_bit_Adder u_3_4_bit_adder_1 (
    .in_1(in_1), .in_2(in_2), .in_3({3'b000, n1_bit_not_1_out_2[0]}), .out_6(out_13));  // open: MSB, out_5
  _3_4_bit_Adder u_3_4_bit_adder_2 (
    .in_1(A_B_prime), .in_2(A_B_t), .in_3({3'b000, n1_bit_not_1_out_2[0]}), .out_6(out_14));  // open: MSB, out_5
  _3_4_bit_Adder u_3_4_bit_adder_3 (
    .in_1(in_1), .in_2(in_2), .in_3({3'b000, n1_bit_not_1_out_2[0]}), .out_6(out_16));  // open: MSB, out_5
  _3_4_bit_Adder u_3_4_bit_adder_4 (
    .in_1(A_B), .in_2(in_1), .in_3({3'b000, n1_bit_not_1_out_2[0]}), .out_6(out_17));  // open: MSB, out_5
  _3_4_bit_Adder u_3_4_bit_adder_5 (
    .in_1(A_B_prime), .in_2(in_1), .in_3({3'b000, n1_bit_not_1_out_2[0]}), .out_6(out_18));  // open: MSB, out_5
  _2_4_bit_Adder u_2_4_bit_adder_2 (.in_1(A_B), .in_2({3'b000, n1_bit_not_1_out_2[0]}), .out_3(out_5));  // open: out_4
  Or or_3 (
    .in_5(in_1[0]), .in_6(in_1[1]), .in_7(in_1[2]), .in_8(in_1[3]), .out_9(A_B_prime[0]),
    .out_10(A_B_prime[1]), .out_11(A_B_prime[2]), .out_12(A_B_prime[3]), .in_1(not_1_out_5[0]),
    .in_3(not_1_out_5[2]), .in_4(not_1_out_5[3]), .in_2(not_1_out_5[1]));
  Subtractor #(.width(4)) subtractor_1 (
    .a(4'b0000), .b({3'b000, n1_bit_not_1_out_2[0]}), .out(out_7));  // open: bin, bout
  And and_2 (
    .in_1(not_2_out_5[0]), .in_2(not_2_out_5[1]), .in_3(not_2_out_5[2]), .in_4(not_2_out_5[3]),
    .in_5(in_1[0]), .in_6(in_1[1]), .in_7(in_1[2]), .in_8(in_1[3]), .out_9(and_2_out_9[0]),
    .out_10(and_2_out_9[1]), .out_11(and_2_out_9[2]), .out_12(and_2_out_9[3]));
  And and_3 (
    .in_1(not_3_out_5[0]), .in_2(not_3_out_5[1]), .in_3(not_3_out_5[2]), .in_4(not_3_out_5[3]),
    .in_5(in_1[0]), .in_6(in_1[1]), .in_7(in_1[2]), .in_8(in_1[3]), .out_9(A_B_prime_t[0]),
    .out_10(A_B_prime_t[1]), .out_11(A_B_prime_t[2]), .out_12(A_B_prime_t[3]));
  Subtractor #(.width(4)) subtractor_2 (.a(in_1), .b(in_2), .out(subtractor_2_out));  // open: bin, bout
  Subtractor #(.width(4)) subtractor_3 (
    .a(A_B_prime_t), .b({3'b000, n1_bit_not_1_out_2[0]}), .out(out_11));  // open: bin, bout
  Subtractor #(.width(4)) subtractor_4 (
    .a(A_B_t), .b({3'b000, n1_bit_not_1_out_2[0]}), .out(out_15));  // open: bin, bout
  Subtractor #(.width(4)) subtractor_5 (
    .a(in_1), .b({3'b000, n1_bit_not_1_out_2[0]}), .out(out_19));  // open: bin, bout
  _2_4_bit_Adder u_2_4_bit_adder_3 (
    .in_1(A_B_prime), .in_2({3'b000, n1_bit_not_1_out_2[0]}), .out_3(out_6));  // open: out_4
  _3_4_bit_Adder u_3_4_bit_adder_6 (
    .in_1(in_1), .in_2(and_2_out_9), .in_3({3'b000, n1_bit_not_1_out_2[0]}), .out_6(out_8));  // open: MSB, out_5
  _3_4_bit_Adder u_3_4_bit_adder_7 (
    .in_1(or_2_out_9), .in_2(A_B_prime_t), .in_3({3'b000, n1_bit_not_1_out_2[0]}), .out_6(out_9));  // open: MSB, out_5
  Subtractor #(.width(4)) subtractor_6 (
    .a(subtractor_2_out), .b({3'b000, n1_bit_not_1_out_2[0]}), .out(out_10));  // open: bin, bout
  _3_4_bit_Adder u_3_4_bit_adder_8 (
    .in_1(in_1), .in_2(A_B_t), .in_3({3'b000, n1_bit_not_1_out_2[0]}), .out_6(out_12));  // open: MSB, out_5
endmodule
